# Fritzing sketch ESP8266_01_Programer (saved by Fritzing 0.9.3b)
breadboards: 1

parts:
  part = ESP8266 WiFi Module [part_number=ESP8266]
  U2 = AMS1117 3.3V Module
  R3 = Resistor [tolerance=±1% resistance=10k package=THT]
  SW1 = Pushbutton [package=THT]
  SW2 = Pushbutton [package=THT]
  FT232RL = FTDI Basic Programmer
  J1 = female pin header, 2 pins [form="♀ (female)"]
  LED1 = LED - 3mm [color="Green (555nm)" package="3 mm [THT]"]
  R2 = Resistor [tolerance=±5% resistance=10k package=THT]
  R1 = Resistor [tolerance=±5% resistance=220 package=THT]

nets:
  N1: part.RXD, FT232RL.TXO
  N2: part.VCC, U2.OUT, R3.Pin_0, R2.Pin_0
  N3: part.GPIO_0, SW1.leg1, J1.pin2
  N4: part.RST, R3.Pin_1, SW2.leg0
  N5: part.GPIO_2, J1.pin1, R1.Pin_0
  N6: part.CH_PD, R2.Pin_1
  GND: part.GND, U2.GND, SW1.leg0, SW2.leg1, FT232RL.GND, LED1.cathode
  N7: part.TXD, FT232RL.RXI
  N8: U2.VIN, FT232RL.POWER
  N9: LED1.anode, R1.Pin_1

notes:
  RESET
  PROGRAM
  GPIO

custom parts:
  ESP8266 WiFi Module: Generic WiFi Module based on the ESP8266 with onboard PCB antenna and UART communications
  AMS1117 3.3V Module: Description: Step Down Power Supply Module AMS1117 3.3v, Input voltage: 4.2 V - 10 V, Output: 3.3 V, 800 mA
